// Logisim project Exercicio4 A-F.circ as structural Verilog: 1 circuit, main circuit main
module main (
  input  A,
  input  A_2,
  input  B,
  input  B_2,
  input  C,
  input  D,
  input  C_2,
  input  E,
  input  D_2,
  input  E_2,
  input  A_3,
  input  B_3,
  input  A_4,
  input  C_3,
  input  B_4,
  input  D_3,
  input  C_4,
  input  E_3,
  input  D_4,
  input  A_5,
  input  A_6,
  input  B_5,
  input  B_6,
  input  C_5,
  input  D_5,
  input  C_6,
  input  E_4,
  input  D_6,
  input  F,
  input  E_5,
  input  G,
  input  H,
  output out_33,
  output out_34,
  output out_35,
  output out_36,
  output out_37
);

  wire and_1_out, and_2_out, and_3_out, and_4_out, and_7_out, and_8_out, and_9_out, and_10_out, and_11_out,
       and_12_out, or_1_out, or_2_out, or_3_out, or_4_out, or_6_out, or_7_out, or_8_out, or_9_out, or_10_out,
       or_12_out, or_14_out;

  and and_1 (and_1_out, A_2, B_2);
  and and_2 (and_2_out, C_2, D_2, E_2);
  and and_3 (and_3_out, C_4, D_4);
  or or_1 (or_1_out, A_6, B_6);
  or or_2 (or_2_out, C_6, D_6);
  or or_3 (or_3_out, B_4, A_4);
  or or_4 (or_4_out, B_4, and_3_out);
  and and_4 (and_4_out, or_1_out, or_2_out);
  or or_5 (out_33, and_1_out, and_2_out);
  or or_6 (or_6_out, A_4, or_4_out);
  and and_5 (out_37, and_4_out, E_5);
  and and_6 (out_35, or_3_out, or_6_out);
  and and_7 (and_7_out, A, B);
  or or_7 (or_7_out, C, D);
  and and_8 (and_8_out, B_5, C_5);
  and and_9 (and_9_out, D_5, E_4);
  and and_10 (and_10_out, F, G);
  and and_11 (and_11_out, and_7_out, or_7_out);
  or or_8 (or_8_out, A_3, B_3);
  or or_9 (or_9_out, C_3, D_3);
  or or_10 (or_10_out, and_8_out, and_9_out);
  or or_11 (out_34, and_11_out, E);
  and and_12 (and_12_out, or_8_out, or_9_out);
  or or_12 (or_12_out, A_5, or_10_out);
  or or_13 (out_36, and_12_out, E_3);
  or or_14 (or_14_out, or_12_out, and_10_out);
  // OR_Gate or_15 has open pins: in0=or_14_out, in1=H, out=open

  // Notes on the sheet:
  //   a)
  //   b)
  //   c)
  //   d)
  //   e)
  //   f)
endmodule
