// Logisim project exercicio 3.circ as structural Verilog: 1 circuit, main circuit main
module main (
  input  in_1,
  input  in_2,
  input  in_3,
  input  in_4,
  input  in_5,
  input  in_6,
  input  in_7,
  input  in_8,
  output out_9,
  output out_10
);

  wire and_1_out, nand_1_out, not_1_out, not_2_out, not_3_out, not_4_out, or_1_out, or_2_out, or_3_out,
       xor_1_out;

  not not_1 (not_1_out, in_1);
  not not_2 (not_2_out, in_7);
  not not_3 (not_3_out, in_2);
  or or_1 (or_1_out, in_3, not_1_out);
  nand nand_1 (nand_1_out, in_4, in_5);
  and and_1 (and_1_out, in_1, not_3_out);
  or or_2 (or_2_out, not_2_out, in_8);
  or or_3 (or_3_out, and_1_out, or_1_out);
  not not_4 (not_4_out, or_1_out);
  xor xor_1 (xor_1_out, nand_1_out, in_6);
  and and_2 (out_10, xor_1_out, or_2_out);
  and and_3 (out_9, or_3_out, not_4_out);
endmodule
