// Logisim project exercicio4 G-K.circ as structural Verilog: 1 circuit, main circuit main
module main (
  input  A,
  input  A_2,
  input  B,
  input  B_2,
  input  C,
  input  C_2,
  input  D,
  input  A_3,
  input  B_3,
  input  C_3,
  input  D_2,
  input  A_4,
  input  B_4,
  input  C_4,
  input  in_15,
  input  in_16,
  input  in_17,
  input  in_18,
  output out_19,
  output out_20,
  output out_21,
  output out_22
);

  wire and_1_out, and_3_out, and_5_out, nor_1_out, nor_2_out, not_1_out, not_2_out, not_3_out, not_4_out,
       not_5_out, not_6_out, or_2_out, or_3_out, or_4_out, or_5_out, xnor_1_out, xnor_2_out, xor_1_out,
       xor_2_out, xor_3_out;

  not not_1 (not_1_out, in_17);
  xor xor_1 (xor_1_out, B_2, C_2);
  nor nor_1 (nor_1_out, A_3, B_3);
  not not_2 (not_2_out, D_2);
  and and_1 (and_1_out, in_15, in_16, not_1_out);
  and and_2 (out_19, A_2, xor_1_out);
  and and_3 (and_3_out, not_2_out, A_3);
  or or_1 (out_22, and_1_out, xnor_1_out);
  xnor xnor_1 (xnor_1_out, not_1_out, in_18);
  xor xor_2 (xor_2_out, C_3, and_3_out);
  and and_4 (out_21, nor_1_out, xor_2_out);
  not not_3 (not_3_out, C);
  not not_4 (not_4_out, C_4);
  not not_5 (not_5_out, B);
  or or_2 (or_2_out, not_3_out, A);
  nor nor_2 (nor_2_out, B, A);
  xor xor_3 (xor_3_out, A_4, B_4);
  or or_3 (or_3_out, A, xnor_2_out);
  xnor xnor_2 (xnor_2_out, not_5_out, D);
  and and_5 (and_5_out, or_3_out, or_2_out);
  or or_4 (or_4_out, xor_3_out, not_4_out);
  not not_6 (not_6_out, A_4);
  or or_5 (or_5_out, and_5_out, B);
  // OR_Gate or_6 has open pins: in0=or_4_out, in1=not_6_out, out=open
  and and_6 (out_20, or_5_out, nor_2_out);

  // Notes on the sheet:
  //   g)
  //   h)
  //   i)
  //   j)
  //   k)
endmodule
